# Fritzing sketch transMotorKnob (saved by Fritzing 0.9.3b)
breadboards: 1

parts:
  Part1 = Arduino Uno (Rev3)
  LED1 = LED - 5mm [color="Red (633nm)" package="5 mm [THT]"]
  M1 = DC Motor
  Q1 = Basic FET P-Channel [package="TO220 [THT]"]
  R1 = Resistor [tolerance=±5% resistance=220 package=THT]
  R2 = Rotary Potentiometer (Small) [maximum_resistance=100kΩ package=THT]
  R3 = Resistor [tolerance=±5% resistance=1k package=THT]
  Power_plug1 = Power plug
  D1 = Rectifier Diode [part_number=1N4148 package="300 mil [THT]"]

nets:
  N1: Part1.A0, R2.wiper
  GND: Part1.GND, Q1.source, R1.Pin_1, R2.leg1, Power_plug1.GND
  N2: Part1.D6_PWM, LED1.anode, R3.Pin_0
  N3: Part1.5V, R2.leg2
  N4: LED1.cathode, R1.Pin_0
  N5: M1.pin_1, Power_plug1.VCC, D1.cathode
  N6: M1.pin_2, Q1.drain, D1.anode
  N7: Q1.gate, R3.Pin_1
