# Fritzing sketch transSolenoidButton (saved by Fritzing 0.9.3b)
breadboards: 1

parts:
  Part1 = Arduino Uno (Rev3)
  LED1 = LED - 5mm [color="Red (633nm)" package="5 mm [THT]"]
  Q1 = Basic FET P-Channel [package="TO220 [THT]"]
  R1 = Resistor [tolerance=±5% resistance=220 package=THT]  # not connected
  Power_plug1 = Power plug
  D1 = Rectifier Diode [part_number=1N4148 package="300 mil [THT]"]
  S1 = Pushbutton [package=THT]
  L1 = Solenoid
  R3 = Resistor [tolerance=±5% resistance=1k package=THT]

nets (from the schematic view):
  N1: Part1.D12/MISO, S1.leg0
  GND: Part1.GND, Q1.source, Power_plug1.GND, S1.leg1
  N2: Part1.D6_PWM, LED1.anode, R3.Pin_0
  N3: Q1.gate, R3.Pin_1
  N4: Q1.drain, D1.anode, L1.pin1
  N5: Power_plug1.VCC, D1.cathode, L1.pin2
